// Logisim project pc.circ as structural Verilog
module ULA (
  input  [15:0] A,
  input  [3:0] F,
  input  [15:0] B,
  output [15:0] R,
  output F_2
);

  wire not_1_out, not_2_out, not_3_out, not_4_out, not_5_out, not_6_out, not_7_out, not_8_out, not_9_out,
       not_10_out, not_11_out, not_12_out, not_13_out, not_14_out, or_1_out, or_2_out, or_3_out, or_4_out,
       or_5_out, or_6_out, or_7_out, or_8_out, or_9_out, or_10_out, or_11_out, or_12_out, or_13_out,
       or_14_out, or_15_out, or_16_out, or_17_out, or_18_out, or_19_out, or_20_out, or_21_out, or_22_out,
       or_23_out, or_24_out, or_25_out, or_26_out, or_27_out;
  wire [15:0] and_2_out, and_3_out, and_4_out, and_5_out, and_6_out, and_7_out, and_8_out, and_9_out,
       and_10_out, resltado_divisao, resultado_and, resultado_left_shift, resultado_multicacao,
       resultado_not, resultado_or, resultado_right_shift, resultado_soma, resultado_subtracao;
  wire [15:15] not_15_out, not_16_out, not_17_out, not_18_out, not_19_out, not_20_out, not_21_out,
       not_22_out, not_23_out;

  not not_1 (not_1_out, F[0]);
  or or_1 (or_1_out, F[2], F[3]);
  not not_2 (not_2_out, F[2]);
  or or_2 (or_2_out, not_2_out, F[3]);
  or or_3 (or_3_out, F[2], not_3_out);
  not not_3 (not_3_out, F[3]);
  not not_4 (not_4_out, F[0]);
  not not_5 (not_5_out, F[1]);
  or or_4 (or_4_out, F[2], F[3]);
  not not_6 (not_6_out, F[0]);
  not not_7 (not_7_out, F[2]);
  or or_5 (or_5_out, not_7_out, F[3]);
  not not_8 (not_8_out, F[1]);
  not not_9 (not_9_out, F[2]);
  or or_6 (or_6_out, not_9_out, F[3]);
  not not_10 (not_10_out, F[0]);
  not not_11 (not_11_out, F[1]);
  not not_12 (not_12_out, F[2]);
  or or_7 (or_7_out, not_12_out, F[3]);
  not not_13 (not_13_out, F[0]);
  or or_8 (or_8_out, F[2], not_14_out);
  not not_14 (not_14_out, F[3]);
  or or_9 (or_9_out, F[0], F[1]);
  or or_10 (or_10_out, or_9_out, or_11_out);
  or or_11 (or_11_out, F[2], F[3]);
  or or_12 (or_12_out, not_1_out, F[1]);
  or or_13 (or_13_out, or_12_out, or_1_out);
  or or_14 (or_14_out, F[0], F[1]);
  or or_15 (or_15_out, or_14_out, or_2_out);
  or or_16 (or_16_out, F[0], F[1]);
  or or_17 (or_17_out, or_16_out, or_3_out);
  or or_18 (or_18_out, not_4_out, not_5_out);
  or or_19 (or_19_out, or_18_out, or_4_out);
  or or_20 (or_20_out, not_6_out, F[1]);
  or or_21 (or_21_out, or_20_out, or_5_out);
  or or_22 (or_22_out, F[0], not_8_out);
  or or_23 (or_23_out, or_22_out, or_6_out);
  or or_24 (or_24_out, not_10_out, not_11_out);
  or or_25 (or_25_out, or_24_out, or_7_out);
  or or_26 (or_26_out, not_13_out, F[1]);
  or or_27 (or_27_out, or_26_out, or_8_out);
  not not_15 (not_15_out[15], or_10_out);
  not not_16 (not_16_out[15], or_13_out);
  not not_17 (not_17_out[15], or_15_out);
  not not_18 (not_18_out[15], or_17_out);
  not not_19 (not_19_out[15], or_19_out);
  not not_20 (not_20_out[15], or_21_out);
  not not_21 (not_21_out[15], or_23_out);
  not not_22 (not_22_out[15], or_25_out);
  not not_23 (not_23_out[15], or_27_out);
  Adder #(.width(16)) adder_1 (.a(A), .b(B), .out(resultado_soma));  // open: cin, cout
  Subtractor #(.width(16)) subtractor_1 (.a(A), .b(B), .out(resultado_subtracao));  // open: bin, bout
  Multiplier #(.width(16)) multiplier_1 (.a(A), .b(B), .out(resultado_multicacao));  // open: cin, cout
  Divider #(.width(16)) divider_1 (.a(A), .b(B), .out(resltado_divisao));  // open: upper, rem
  assign resultado_and = A & B;  // AND_Gate and_1, 16 bits wide
  assign resultado_or = A | B;  // OR_Gate or_28, 16 bits wide
  assign resultado_not = ~A;  // NOT_Gate not_24, 16 bits wide
  Shifter #(.width(16)) shifter_1 (.in(A), .\dist (B[3:0]), .out(resultado_left_shift));
  Shifter #(.width(16), .shift("lr")) shifter_2 (.in(A), .\dist (B[3:0]), .out(resultado_right_shift));
  Comparator #(.width(16), .mode("unsigned")) comparator_1 (.a(A), .b(B), .gt(F_2));  // open: eq, lt
  assign and_2_out = {16{not_15_out[15]}} & resultado_soma;  // AND_Gate and_2, 16 bits wide
  assign and_3_out = {16{not_16_out[15]}} & resultado_subtracao;  // AND_Gate and_3, 16 bits wide
  assign and_4_out = {16{not_17_out[15]}} & resultado_multicacao;  // AND_Gate and_4, 16 bits wide
  assign and_5_out = {16{not_18_out[15]}} & resltado_divisao;  // AND_Gate and_5, 16 bits wide
  assign and_6_out = {16{not_19_out[15]}} & resultado_and;  // AND_Gate and_6, 16 bits wide
  assign and_7_out = {16{not_20_out[15]}} & resultado_or;  // AND_Gate and_7, 16 bits wide
  assign and_8_out = {16{not_21_out[15]}} & resultado_not;  // AND_Gate and_8, 16 bits wide
  assign and_9_out = {16{not_22_out[15]}} & resultado_left_shift;  // AND_Gate and_9, 16 bits wide
  assign and_10_out = {16{not_23_out[15]}} & resultado_right_shift;  // AND_Gate and_10, 16 bits wide
  assign R = and_2_out | and_3_out | and_4_out | and_5_out | and_6_out | and_7_out | and_8_out | and_9_out | and_10_out;  // OR_Gate or_29, 16 bits wide

  // Other names for the same wires on the sheet: b0 = F[0]; b1 = F[1]; b2 = F[2]; b3 = F[3]
endmodule

module Registradores (
  input  [15:0] D,
  input  [4:0] A1,
  input  [4:0] A2,
  input  C,
  input  R,
  input  E,
  output [15:0] O1,
  output [15:0] O2
);

  Decoder #(.select(5)) decoder_1 ();  // open: out0, out1, out2, out3, out4, out5, out6, out7, out8, out9, out10, out11, out12, out13, out14, out15, out16, out17, out18, out19, out20, out21, out22, out23, out24, out25, out26, out27, out28, out29, out30, out31, sel, en
  Register #(.width(16)) register_1 ();  // open: D, en, Q, clk, clr
  Register #(.width(16)) register_2 ();  // open: D, en, Q, clk, clr
  Register #(.width(16)) register_3 ();  // open: D, en, Q, clk, clr
  Register #(.width(16)) register_4 ();  // open: D, en, Q, clk, clr
  Register #(.width(16)) register_5 ();  // open: D, en, Q, clk, clr
  Register #(.width(16)) register_6 ();  // open: D, en, Q, clk, clr
  Register #(.width(16)) register_7 ();  // open: D, en, Q, clk, clr
  Register #(.width(16)) register_8 ();  // open: D, en, Q, clk, clr
  Register #(.width(16)) register_9 ();  // open: D, en, Q, clk, clr
  Register #(.width(16)) register_10 ();  // open: D, en, Q, clk, clr
  Register #(.width(16)) register_11 ();  // open: D, en, Q, clk, clr
  Register #(.width(16)) register_12 ();  // open: D, en, Q, clk, clr
  Register #(.width(16)) register_13 ();  // open: D, en, Q, clk, clr
  Register #(.width(16)) register_14 ();  // open: D, en, Q, clk, clr
  Register #(.width(16)) register_15 ();  // open: D, en, Q, clk, clr
  Register #(.width(16)) register_16 ();  // open: D, en, Q, clk, clr
  Register #(.width(16)) register_17 ();  // open: D, en, Q, clk, clr
  Register #(.width(16)) register_18 ();  // open: D, en, Q, clk, clr
  Register #(.width(16)) register_19 ();  // open: D, en, Q, clk, clr
  Register #(.width(16)) register_20 ();  // open: D, en, Q, clk, clr
  Register #(.width(16)) register_21 ();  // open: D, en, Q, clk, clr
  Register #(.width(16)) register_22 ();  // open: D, en, Q, clk, clr
  Register #(.width(16)) register_23 ();  // open: D, en, Q, clk, clr
  Register #(.width(16)) register_24 ();  // open: D, en, Q, clk, clr
  Register #(.width(16)) register_25 ();  // open: D, en, Q, clk, clr
  Register #(.width(16)) register_26 ();  // open: D, en, Q, clk, clr
  Register #(.width(16)) register_27 ();  // open: D, en, Q, clk, clr
  Register #(.width(16)) register_28 ();  // open: D, en, Q, clk, clr
  Register #(.width(16)) register_29 ();  // open: D, en, Q, clk, clr
  Register #(.width(16)) register_30 ();  // open: D, en, Q, clk, clr
  Register #(.width(16)) register_31 ();  // open: D, en, Q, clk, clr
  Register #(.width(16)) register_32 ();  // open: D, en, Q, clk, clr
  Multiplexer #(.select(5), .width(16)) multiplexer_1 ();  // open: in0, in1, in2, in3, in4, in5, in6, in7, in8, in9, in10, in11, in12, in13, in14, in15, in16, in17, in18, in19, in20, in21, in22, in23, in24, in25, in26, in27, in28, in29, in30, in31, out, sel, en
endmodule
